# Fritzing sketch mtg-scan (saved by Fritzing 0.9.3b)
breadboards: 1

parts:
  MASTER = Arduino Uno (Rev3)
  VCC1 = Battery  # not connected
  J1 = Basic Servo  # not connected
  M1 = DC Motor  # not connected
  LED1 = LED - 5mm [color="Green (555nm)" package="5 mm [THT]"]  # not connected
  LED2 = LED - 5mm [color="Yellow (595nm)" package="5 mm [THT]"]  # not connected
  R1 = Resistor [tolerance=±5% resistance=3.30k package=THT]  # not connected
  R2 = Resistor [tolerance=±5% resistance=3.30k package=THT]  # not connected
  S1 = Pushbutton [package="[THT]"]  # not connected
  S2 = Toggle Switch [package=THT]  # not connected
  S3 = Pushbutton [package="[THT]"]  # not connected
  S4 = Pushbutton [package="[THT]"]  # not connected
  S5 = Pushbutton [package="[THT]"]  # not connected
  S6 = Toggle Switch [package=THT]  # not connected
  U2 = 640x480 CMOS Color Camera [package=camera_cmos_con]  # not connected
  SLAVE = Arduino Uno (Rev3)

nets:
  N1: MASTER.A4/SDA, SLAVE.A4/SDA
  N2: MASTER.A5/SCL, SLAVE.A5/SCL

// code stored in the sketch: arducam-debug.ino
#include <Wire.h>
#include <BreezyArduCAM.h>
#include <SPI.h>

// CAMERA
const int CS_CAM = 10;

// BUTTONS
const int BUTTON = 7;

// LEDS
const int LED = 8;

const long SERIAL_SPEED = 921600; //921600


Serial_ArduCAM_FrameGrabber fg;
ArduCAM_Mini_2MP cardCam(CS_CAM, &fg);


void setup(void)
{
  Wire.begin();
  SPI.begin();

  Serial.begin(SERIAL_SPEED);
  cardCam.beginJpeg800x600();

  pinMode(BUTTON, INPUT_PULLUP);
  pinMode(LED, OUTPUT);
}

bool capturing = false;
void loop(void)
{
  if (digitalRead(BUTTON) == LOW) {
    digitalWrite(LED, HIGH);
    cardCam.singleCapture();
  } else {
    digitalWrite(LED, LOW);
  }
}

// code stored in the sketch: lcd.ino
//YWROBOT
//Compatible with the Arduino IDE 1.0
//Library version:1.1
#include <LiquidCrystal_I2C.h>

LiquidCrystal_I2C lcd(0x3F,20,4);  // set the LCD address to 0x27 for a 16 chars and 2 line display

void setup()
{
  lcd.init();                      // initialize the lcd 
  // Print a message to the LCD.
  lcd.backlight();
  lcd.setCursor(3,0);
  lcd.print("Hello, world!");
  lcd.setCursor(2,1);
  lcd.print("Ywrobot Arduino!");
   lcd.setCursor(0,2);
  lcd.print("Arduino LCM IIC 2004");
   lcd.setCursor(2,3);
  lcd.print("Power By Ec-yuan!");
}


void loop()
{
}

// code stored in the sketch: master.ino
#include <Wire.h>
#include <BreezyArduCAM.h>
#include <LiquidCrystal_I2C.h>
#include <SPI.h>

// CAMERA
const int CS_CAM = 10;

// BUTTONS
const int BUTTON_A = 7;
const int BUTTON_B = 6;
const int BUTTON_C = 5;
const int BUTTON_D = 4;
const int SWITCH = 3;

// LEDS
const int LED_GREEN = A0;
const int LED_WHITE = A1;
const int LED_YELLOW = A2;
const int LED_BLUE = A3;

// CONST
const int SEND_CARD = 1;
const int OPEN_SERVO = 2;

// SERIAL
const long SERIAL_SPEED = 921600; //921600
const int ARDUINO_ADDRESS = 8;
const int SLAVE_ADDRESS = 8;
const uint8_t LCD_ADDRESS = 0x3F;

// CARD COLORS
const char CARD_NONE = 'N';
const char CARD_UNKNOWN = 'X';
const char CARD_RED = 'R';
const char CARD_GREEN = 'G';
const char CARD_BLUE = 'U';
const char CARD_BLACK = 'B';
const char CARD_WHITE = 'W';
const char CARD_COLORLESS = 'C';
const char CARD_OTHER = 'O';


Serial_ArduCAM_FrameGrabber fg;
ArduCAM_Mini_2MP cardCam(CS_CAM, &fg);

LiquidCrystal_I2C lcd(LCD_ADDRESS,20,4);

void setup(void)
{
  Wire.begin();
  SPI.begin();

  Serial.begin(SERIAL_SPEED);
  cardCam.beginJpeg800x600();

  lcd.init();
  lcd.backlight();

  pinMode(BUTTON_A, INPUT_PULLUP);
  pinMode(BUTTON_B, INPUT_PULLUP);
  pinMode(BUTTON_C, INPUT_PULLUP);
  pinMode(BUTTON_D, INPUT_PULLUP);
  pinMode(SWITCH, INPUT_PULLUP);

  pinMode(LED_GREEN, OUTPUT);
  pinMode(LED_WHITE, OUTPUT);
  pinMode(LED_YELLOW, OUTPUT);
  pinMode(LED_BLUE, OUTPUT);

  intro();
}

void intro(void){
  int i, j;
  int leds[] = {LED_GREEN, LED_WHITE, LED_YELLOW, LED_BLUE};
  for (i = 0; i < 4; i++) {
    if (i > 0) {
      digitalWrite(leds[i-1], LOW);
    }
    digitalWrite(leds[i], HIGH);
    delay(70);
  }
  for (i = 3; i >= 0 ; i--) {
    if (i < 4) {
      digitalWrite(leds[i+1], LOW);
    }
    digitalWrite(leds[i], HIGH);
    delay(70);
  }
  for (i = 0; i < 4; i++) {
    digitalWrite(leds[i], HIGH);
    delay(70);
  }
  
  for (i = 0; i < 4; i++) {
    for (j = 0; j < 4; j++) {
      digitalWrite(leds[j], HIGH);
    }
    delay(100);
    for (j = 0; j < 4; j++) {
      digitalWrite(leds[j], LOW);
    }
    delay(100);
  }
}

enum states {
  None,
  Send,
  Capture,
  Analyze,
  Sort
};
states state = Send;

void sendToSlave(byte value)
{
  Wire.beginTransmission(SLAVE_ADDRESS);
  Wire.write(value);
  Wire.endTransmission();
}
unsigned long startcaptureTime;

bool modeAuto = false;
char cardColor = CARD_NONE;
void loop(void)
{
  buttonA();
  buttonB();
  buttonC();
  buttonD();

  if (digitalRead(SWITCH) == HIGH) {
    modeAuto = false;
    state = Send;
    digitalWrite(LED_GREEN, LOW);
		printLcdLine("Mode: manual", 0);
  } else {
    modeAuto = true;
    digitalWrite(LED_GREEN, HIGH);
		printLcdLine("Mode: auto", 0);
  }

  if (modeAuto) {
    switch (state) {
      case Send:
        {
          cardColor = CARD_NONE;
         	sendCard();
          state = Capture;
        }
        break;
      case Capture:
        {
         	if (!captureCard()) {
            cardColor = CARD_UNKNOWN;
            state = Sort;
          } else {
            state = Analyze;
          }
        }
        break;
      case Analyze:
        {
          analyzeCard();
        }
        break;
      case Sort:
        {
          sortCard();
          state = Send;
        }
        break;
    }
  }

}

void printLcdLine(char message[], int line)
{
  char str[21];

  sprintf(str, "%-20s", message);
  lcd.setCursor(0, line);
  lcd.print(str);
}

void clearLcdLine(int line)
{
  lcd.setCursor(0, line);
  lcd.print("                    ");
}

void sendCard(void)
{
  clearLcdLine(1);
  clearLcdLine(2);
  clearLcdLine(3);
	printLcdLine("Sending card...", 1);
  sendToSlave(SEND_CARD);
	delay(1000);
  clearLcdLine(1);
}

bool captureCard(void)
{
  clearLcdLine(1);
  clearLcdLine(2);
  clearLcdLine(3);
	printLcdLine("Capturing card...", 1);
  digitalWrite(LED_YELLOW, HIGH);
  //bool status = cardCam.singleCapture();
  bool status = true;
  delay(1000);
  digitalWrite(LED_YELLOW, LOW);
  if (!status) {
	  printLcdLine("Capture error!", 2);
  } else {
	  printLcdLine("Capture success", 2);
  }
  clearLcdLine(1);

  return status;
}

bool analyzing = false;
void analyzeCard(void)
{
  if (!analyzing) {
    analyzing = true;
    clearLcdLine(1);
    clearLcdLine(2);
    clearLcdLine(3);
    printLcdLine("Analyzing card...", 1);
  }
  delay(1000);
  //if (analyzing && Serial.available()) {
    //String color = Serial.readString();
  if (analyzing) {
    char color = "R";
    
    state = Sort;
    
    char cardMsg[21];
    sprintf(cardMsg, "Card is: %c", color);
    printLcdLine(cardMsg, 3);
    clearLcdLine(1);
    analyzing = false;
  }
}

void sortCard(void)
{
  clearLcdLine(1);
  clearLcdLine(2);
  clearLcdLine(3);
	printLcdLine("Sorting card...", 1);
  sendToSlave(OPEN_SERVO);
  delay(500);
  clearLcdLine(1);
}


void buttonA()
{
  if (digitalRead(BUTTON_A) == LOW) {
    sendCard();
  }
}

void buttonB()
{
  if (digitalRead(BUTTON_B) == LOW) {
    captureCard();
  }
}

void buttonC(void) {
  if (digitalRead(BUTTON_C) == LOW) {
    sortCard();
  }
}

void buttonD(void) {
}

// code stored in the sketch: slave.ino
#include <Servo.h>
#include <Wire.h>

Servo cardServo;

// MOTORS
const int MOTOR_CARD_FORWARD = 9;
const int MOTOR_CARD_BACKWARD = 10;
const int MOTOR_CARD_PWM = 11;
const int MOTOR_CARD_FORWARD_TIME = 600; //ms
const int MOTOR_CARD_BACKWARD_TIME = 130; //ms
const int SERVO_CARD = 2;
const int SERVO_CLOSE = 60;
const int SERVO_OPEN = 130;
const int SERVO_OPEN_TIME = 250; //ms

// SERIAL
const long SERIAL_SPEED = 921600; //921600
const int ARDUINO_ADDRESS = 8;

// CARD COLORS
const int CARD_NONE = 0;
const int CARD_UNKNOWN = -1;
const int CARD_RED = 1;
const int CARD_GREEN = 2;
const int CARD_BLUE = 3;
const int CARD_BLACK = 4;
const int CARD_WHITE = 5;
const int CARD_COLORLESS = 6;
const int CARD_OTHER = 7;

void setup(void)
{
  Serial.begin(SERIAL_SPEED);

  pinMode(MOTOR_CARD_FORWARD, OUTPUT);
  pinMode(MOTOR_CARD_BACKWARD, OUTPUT);
  pinMode(MOTOR_CARD_PWM, OUTPUT);
  pinMode(SERVO_CARD, OUTPUT);

  cardServo.attach(SERVO_CARD);
  cardServo.write(SERVO_CLOSE);

  Wire.begin(ARDUINO_ADDRESS);
  Wire.onReceive(receiveEvent);
}

bool send_card = false;
bool sort_card = false;
void receiveEvent(int howMany) {
  int x = Wire.read();
  if (x == 1) {
    send_card = true;
  } else if (x == 2) {
    sort_card = true;
  }
}

bool serving_new_card = false;
bool prepare_new_card = false;
unsigned long serving_card_start = 0;
void sendCardtoAnalyse(void)
{
  if (!serving_new_card && !prepare_new_card && send_card) {
    serving_new_card = true;
    serving_card_start = millis();
    analogWrite(MOTOR_CARD_FORWARD, 255);
    analogWrite(MOTOR_CARD_BACKWARD, 0);
    analogWrite(MOTOR_CARD_PWM, 90);
  }

  if (serving_new_card && (millis() - serving_card_start) > MOTOR_CARD_FORWARD_TIME) {
    serving_new_card = false;
    prepare_new_card = true;
    analogWrite(MOTOR_CARD_FORWARD, 0);
    analogWrite(MOTOR_CARD_BACKWARD, 255);
    analogWrite(MOTOR_CARD_PWM, 255);
  }

  if (prepare_new_card && (millis() - serving_card_start) > MOTOR_CARD_FORWARD_TIME + MOTOR_CARD_BACKWARD_TIME) {
    send_card = false;
    prepare_new_card = false;
    analogWrite(MOTOR_CARD_FORWARD, 0);
    analogWrite(MOTOR_CARD_BACKWARD, 0);
  }
}

bool sorting_card = false;
unsigned long sorting_card_start = 0;
void sendCardToSorting()
{
  if (!sorting_card && sort_card) {
    sorting_card = true;
    sort_card = false;
    sorting_card_start = millis();
    cardServo.write(SERVO_OPEN);
  }

  if (sorting_card && (millis() - sorting_card_start) > SERVO_OPEN_TIME) {
    sorting_card = false;
    cardServo.write(SERVO_CLOSE);
  }
}

void loop(void)
{
  sendCardtoAnalyse();
  sendCardToSorting();
}
